// Logisim project 16bitGPU3.circ as structural Verilog: 1 circuit, main circuit main
module main (
);

  wire and_1_out, and_2_out, and_3_out, and_4_out, and_5_out, and_6_out, and_7_out, and_8_out, and_9_out,
       and_10_out, and_11_out, and_12_out, and_13_out, and_14_out, and_15_out, clock_1_out, clock_2_out,
       clock_3_out, clock_4_out, clock_5_out, comparator_1_eq, comparator_1_gt, comparator_1_lt,
       comparator_2_lt, comparator_3_gt, comparator_4_gt, comparator_5_lt, comparator_6_eq, comparator_7_eq,
       comparator_8_lt, comparator_9_eq, comparator_10_eq, comparator_11_eq, comparator_11_gt,
       comparator_11_lt, comparator_12_eq, comparator_13_eq, comparator_14_eq, comparator_14_gt,
       comparator_14_lt, comparator_15_lt, comparator_16_eq, comparator_17_eq, dipswitch_1_sw1,
       dipswitch_1_sw2, multiplexer_21_out, multiplexer_24_out, multiplexer_40_out, multiplexer_41_out,
       not_1_out, not_2_out, not_3_out, not_4_out, not_5_out, not_6_out, not_7_out, or_1_out, or_2_out,
       or_3_out, or_4_out, register_1_q, register_2_q, register_3_q, register_4_q, register_5_q,
       register_6_q, xor_1_out, xor_2_out, xor_3_out, xor_4_out;
  wire [4:0] rgb_video_1_p1;
  wire [5:0] multiplexer_18_out, multiplexer_20_out, X_q, X_SUB_q, Y_CNT_q;
  wire [7:0] counter_1_q, counter_3_q;
  wire [15:0] adder_1_out, adder_2_out, adder_3_out, adder_4_out, adder_5_out, adder_6_out, adder_7_out,
       adder_8_out, adder_9_out, adder_10_out, counter_2_q, counter_4_q, D2_q, D2_SUB_q, D_q, D_Sub_q,
       divider_1_out, divider_2_out, divider_3_out, divider_4_out, DX2_p1, DX_p1, DX_REG_q, DY2_p1, DY_p1,
       DY_REG_q, multiplexer_1_out, multiplexer_2_out, multiplexer_3_out, multiplexer_4_out,
       multiplexer_5_out, multiplexer_6_out, multiplexer_7_out, multiplexer_8_out, multiplexer_9_out,
       multiplexer_10_out, multiplexer_11_out, multiplexer_12_out, multiplexer_13_out, multiplexer_14_out,
       multiplexer_15_out, multiplexer_16_out, multiplexer_17_out, multiplexer_25_out, multiplexer_26_out,
       multiplexer_27_out, multiplexer_28_out, multiplexer_29_out, multiplexer_30_out, multiplexer_31_out,
       multiplexer_32_out, multiplexer_33_out, multiplexer_34_out, multiplexer_35_out, multiplexer_36_out,
       multiplexer_37_out, multiplexer_38_out, multiplexer_39_out, multiplier_1_out, multiplier_2_out,
       multiplier_3_out, multiplier_4_out, multiplier_5_out, multiplier_6_out, multiplier_7_out,
       multiplier_8_out, multiplier_9_out, multiplier_10_out, negator_1_out, negator_2_out, rom_1_data_2,
       rom_3_data_2, subtractor_1_out, subtractor_3_out, subtractor_4_out, subtractor_6_out,
       subtractor_7_out, subtractor_10_out, undriven, XI_q, XREG_q, Y_q, Y_sub_q, YI_q;
  wire [15:6] X_q_2, X_SUB_q_2, Y_CNT_q_2;
  wire [16:0] rom_2_data, rom_5_data;
  wire [23:0] multiplexer_19_out;
  wire [31:0] rom_1_data, rom_3_data;

  Subtractor #(.width(16)) subtractor_1 (
    .a(divider_3_out), .b(divider_1_out), .out(subtractor_1_out));  // open: bin, bout
  // LedBar #(.inputtype("row"), .matrixcols(16)) DX: pin names not known; wires that end beside it: DX_p1
  Multiplexer #(.width(16)) multiplexer_1 (
    .in0(divider_1_out), .in1(divider_3_out), .out(multiplexer_1_out), .sel(and_7_out));
  Multiplexer #(.width(16)) multiplexer_2 (
    .in0(divider_2_out), .in1(divider_4_out), .out(multiplexer_2_out), .sel(and_7_out));
  Multiplexer #(.width(16)) multiplexer_3 (
    .in0(divider_3_out), .in1(divider_1_out), .out(multiplexer_3_out), .sel(and_7_out));
  Multiplexer #(.width(16)) multiplexer_4 (
    .in0(divider_4_out), .in1(divider_2_out), .out(multiplexer_4_out), .sel(and_7_out));
  Subtractor #(.width(16)) subtractor_2 (
    .a(multiplexer_11_out), .b(multiplexer_5_out), .out(DX_p1));  // open: bin, bout
  Negator #(.width(16)) negator_1 (.in(DY_p1), .out(negator_1_out));
  Subtractor #(.width(16)) subtractor_3 (.a(DY_REG_q), .b(DX_p1), .out(subtractor_3_out));  // open: bin, bout
  Multiplier #(.mode("twosComplement"), .width(16)) multiplier_1 (
    .a(subtractor_3_out), .b(16'h2), .out(multiplier_1_out));  // open: cin, cout
  Adder #(.width(16)) adder_1 (.a(multiplier_1_out), .b(D_Sub_q), .out(adder_1_out));  // open: cin, cout
  Adder #(.width(16)) adder_2 (.a(D_Sub_q), .b(multiplier_5_out), .out(adder_2_out));  // open: cin, cout
  Comparator #(.width(16)) comparator_1 (
    .a(D_Sub_q), .b({16{1'b0}}), .gt(comparator_1_gt), .eq(comparator_1_eq), .lt(comparator_1_lt));
  Multiplier #(.mode("twosComplement"), .width(16)) multiplier_2 (
    .a(undriven), .b(rom_1_data[15:0]), .out(multiplier_2_out));  // open: cin, cout
  Adder #(.width(16)) adder_3 (.a(undriven), .b(rom_1_data_2), .out(adder_3_out));  // open: cin, cout
  Multiplier #(.mode("twosComplement"), .width(16)) multiplier_3 (
    .a(rom_1_data[31:16]), .b(undriven), .out(multiplier_3_out));  // open: cin, cout
  Adder #(.width(16)) adder_4 (.a(rom_1_data_2), .b(undriven), .out(adder_4_out));  // open: cin, cout
  Comparator #(.width(16)) comparator_2 (.a(subtractor_1_out), .b({16{1'b0}}), .lt(comparator_2_lt));  // open: gt, eq
  Multiplexer #(.width(16)) multiplexer_5 (
    .in0({16{1'b0}}), .in1(multiplexer_1_out), .out(multiplexer_5_out), .sel(rgb_video_1_p1[4]));
  Multiplexer #(.width(16)) multiplexer_6 (.in0(DY_p1), .in1(negator_1_out), .out(multiplexer_6_out), .sel(and_3_out));
  Multiplexer #(.width(16)) multiplexer_7 (
    .in0(D_Sub_q), .in1(adder_1_out), .out(multiplexer_7_out), .sel(register_1_q));
  Adder #(.width(16)) adder_5 (.a(Y_sub_q), .b(YI_q), .out(adder_5_out));  // open: cin, cout
  Register #(.width(1)) register_1 (
    .D(comparator_1_gt), .en(1'b1), .clk(clock_1_out), .Q(register_1_q), .clr(and_10_out));
  Register #(.width(1)) register_2 (
    .D(comparator_1_eq), .en(1'b1), .clk(clock_1_out), .Q(register_2_q), .clr(and_10_out));
  Register #(.width(1)) register_3 (
    .D(comparator_1_lt), .en(1'b1), .clk(clock_1_out), .Q(register_3_q), .clr(and_10_out));
  Divider #(.mode("twosComplement"), .width(16)) divider_1 (
    .a(multiplier_2_out), .b(adder_3_out), .out(divider_1_out));  // open: upper, rem
  Divider #(.mode("twosComplement"), .width(16)) divider_2 (
    .a(multiplier_3_out), .b(adder_4_out), .out(divider_2_out));  // open: upper, rem
  Subtractor #(.width(16)) subtractor_4 (
    .a(divider_4_out), .b(divider_2_out), .out(subtractor_4_out));  // open: bin, bout
  Multiplier #(.mode("twosComplement"), .width(16)) multiplier_4 (
    .a(subtractor_1_out), .b(multiplexer_8_out), .out(multiplier_4_out));  // open: cin, cout
  Multiplexer #(.width(16)) multiplexer_8 (
    .in0(16'h1), .in1({16{1'b1}}), .out(multiplexer_8_out), .sel(comparator_2_lt));
  Comparator #(.width(16)) comparator_3 (.a(divider_1_out), .b(divider_3_out), .gt(comparator_3_gt));  // open: eq, lt
  Comparator #(.width(16)) comparator_4 (.a(divider_2_out), .b(divider_4_out), .gt(comparator_4_gt));  // open: eq, lt
  Multiplexer #(.width(16)) multiplexer_9 (
    .in0({16{1'b0}}), .in1(multiplexer_2_out), .out(multiplexer_9_out), .sel(rgb_video_1_p1[4]));
  // LedBar #(.inputtype("row"), .matrixcols(16)) DY: pin names not known; wires that end beside it: DY_p1
  Comparator #(.width(16)) comparator_5 (.a(DY_p1), .b({16{1'b0}}), .lt(comparator_5_lt));  // open: gt, eq
  Register #(.width(16)) DY_REG (
    .D(multiplexer_6_out), .en(rom_2_data[3]), .clk(clock_1_out), .Q(DY_REG_q));  // open: clr
  Multiplier #(.mode("twosComplement"), .width(16)) multiplier_5 (
    .a(DY_REG_q), .b(16'h2), .out(multiplier_5_out));  // open: cin, cout
  Multiplexer #(.width(16)) multiplexer_10 (
    .in0(Y_sub_q), .in1(adder_5_out), .out(multiplexer_10_out), .sel(and_1_out));
  and and_1 (and_1_out, rom_2_data[12], register_1_q);
  Comparator #(.width(16)) comparator_6 (.a(divider_1_out), .b({16{1'b0}}), .eq(comparator_6_eq));  // open: gt, lt
  Comparator #(.width(16)) comparator_7 (.a(divider_2_out), .b({16{1'b0}}), .eq(comparator_7_eq));  // open: gt, lt
  Multiplexer #(.width(16)) multiplexer_11 (
    .in0({16{1'b0}}), .in1(multiplexer_3_out), .out(multiplexer_11_out), .sel(rgb_video_1_p1[4]));
  Multiplexer #(.width(16)) multiplexer_12 (
    .in0({16{1'b0}}), .in1(multiplexer_4_out), .out(multiplexer_12_out), .sel(rgb_video_1_p1[4]));
  Subtractor #(.width(16)) subtractor_5 (
    .a(multiplexer_12_out), .b(multiplexer_9_out), .out(DY_p1));  // open: bin, bout
  and and_2 (and_2_out, rom_2_data[2], comparator_5_lt);
  and and_3 (and_3_out, comparator_5_lt, rom_2_data[4]);
  Subtractor #(.width(16)) subtractor_6 (.a(multiplier_5_out), .b(DX_p1), .out(subtractor_6_out));  // open: bin, bout
  Multiplexer #(.width(16)) multiplexer_13 (
    .in0(multiplexer_7_out), .in1(multiplexer_14_out), .out(multiplexer_13_out), .sel(rom_2_data[16]));
  Multiplexer #(.width(16)) multiplexer_14 (.in0(D_q), .in1(adder_2_out), .out(multiplexer_14_out), .sel(or_1_out));
  or or_1 (or_1_out, register_2_q, register_3_q);
  Comparator #(.width(16)) comparator_8 (.a(subtractor_4_out), .b({16{1'b0}}), .lt(comparator_8_lt));  // open: gt, eq
  Multiplexer #(.width(16)) multiplexer_15 (
    .in0(16'h1), .in1({16{1'b1}}), .out(multiplexer_15_out), .sel(comparator_8_lt));
  or or_2 (or_2_out, comparator_11_gt, comparator_11_eq);
  and and_4 (and_4_out, or_2_out, comparator_4_gt);
  and and_5 (and_5_out, comparator_6_eq, comparator_7_eq);
  Comparator #(.width(16)) comparator_9 (.a(divider_3_out), .b({16{1'b0}}), .eq(comparator_9_eq));  // open: gt, lt
  and and_6 (and_6_out, comparator_9_eq, comparator_10_eq);
  Comparator #(.width(16)) comparator_10 (.a(divider_4_out), .b({16{1'b0}}), .eq(comparator_10_eq));  // open: gt, lt
  Multiplexer #(.width(16)) multiplexer_16 (
    .in0(subtractor_6_out), .in1(multiplexer_13_out), .out(multiplexer_16_out), .sel(rom_2_data[15]));
  Multiplexer #(.width(16)) multiplexer_17 (
    .in0(multiplexer_9_out), .in1(multiplexer_10_out), .out(multiplexer_17_out), .sel(rom_2_data[12]));
  Multiplier #(.mode("twosComplement"), .width(16)) multiplier_6 (
    .a(undriven), .b(rom_3_data[15:0]), .out(multiplier_6_out));  // open: cin, cout
  Adder #(.width(16)) adder_6 (.a(undriven), .b(rom_3_data_2), .out(adder_6_out));  // open: cin, cout
  Multiplier #(.mode("twosComplement"), .width(16)) multiplier_7 (
    .a(rom_3_data[31:16]), .b(undriven), .out(multiplier_7_out));  // open: cin, cout
  Adder #(.width(16)) adder_7 (.a(rom_3_data_2), .b(undriven), .out(adder_7_out));  // open: cin, cout
  Multiplier #(.mode("twosComplement"), .width(16)) multiplier_8 (
    .a(subtractor_4_out), .b(multiplexer_15_out), .out(multiplier_8_out));  // open: cin, cout
  Comparator #(.width(16)) comparator_11 (
    .a(multiplier_8_out), .b(multiplier_4_out), .gt(comparator_11_gt), .eq(comparator_11_eq),
    .lt(comparator_11_lt));
  and and_7 (and_7_out, or_3_out, comparator_3_gt);
  and and_8 (and_8_out, and_5_out, and_6_out);
  Counter #(.max('hffff), .width(16)) YI (
    .clr(rom_2_data[1]), .up(not_1_out), .clk(xor_1_out), .Q(YI_q));  // open: load, count, D, carry
  not not_1 (not_1_out, and_2_out);
  Register #(.width(16)) D (.D(multiplexer_16_out), .en(rom_2_data[5]), .clk(clock_1_out), .Q(D_q));  // open: clr
  Register #(.width(16)) Y (.D(multiplexer_17_out), .en(and_9_out), .clk(clock_1_out), .Q(Y_q));  // open: clr
  and and_9 (and_9_out, rom_2_data[11], not_3_out);
  Divider #(.mode("twosComplement"), .width(16)) divider_3 (
    .a(multiplier_6_out), .b(adder_6_out), .out(divider_3_out));  // open: upper, rem
  Divider #(.mode("twosComplement"), .width(16)) divider_4 (
    .a(multiplier_7_out), .b(adder_7_out), .out(divider_4_out));  // open: upper, rem
  or or_3 (or_3_out, comparator_11_eq, comparator_11_lt);
  not not_2 (not_2_out, and_8_out);
  Register #(.width(16)) D_Sub (.D(D_q), .en(rom_2_data[14]), .clk(clock_1_out), .Q(D_Sub_q));  // open: clr
  Register #(.width(16)) Y_sub (.D(Y_q), .en(rom_2_data[13]), .clk(clock_1_out), .Q(Y_sub_q));  // open: clr
  Clock clock_1 (.out(clock_1_out));
  xor xor_1 (xor_1_out, rom_2_data[0], and_2_out);
  not not_3 (not_3_out, comparator_12_eq);
  Comparator #(.width(16)) comparator_12 (.a(Y_sub_q), .b(multiplexer_12_out), .eq(comparator_12_eq));  // open: gt, lt
  and and_10 (and_10_out, rom_2_data[1], rom_2_data[10]);
  Multiplexer #(.enable("true"), .width(6)) multiplexer_18 (
    .in0(X_SUB_q), .in1(X_q), .out(multiplexer_18_out), .sel(or_3_out), .en(not_2_out));
  Multiplexer #(.enable("true"), .width(24)) multiplexer_19 (
    .in0({24{1'b1}}), .in1({24{1'b1}}), .out(multiplexer_19_out), .sel(or_3_out), .en(not_2_out));
  Multiplexer #(.enable("true"), .width(6)) multiplexer_20 (
    .in0(Y_CNT_q), .in1(Y_sub_q[5:0]), .out(multiplexer_20_out), .sel(or_3_out), .en(not_2_out));
  Multiplexer #(.enable("true")) multiplexer_21 (
    .in0(rom_5_data[9]), .in1(rom_2_data[9]), .out(multiplexer_21_out), .sel(or_3_out), .en(not_2_out));
  Multiplexer multiplexer_22 (.in0(rom_5_data[10]), .in1(rom_2_data[10]), .sel(or_3_out));  // open: out
  Counter #(.max('hffff), .width(16)) X (
    .clr(xor_2_out), .load(rom_2_data[8]), .count(not_4_out), .clk(rom_2_data[7]), .D(multiplexer_5_out),
    .Q({X_q_2, X_q}));  // open: up, carry
  LED led_1 (.in(register_1_q));
  buf xor_2 (xor_2_out, rom_2_data[6]);  // XOR_Gate
  LED led_2 (.in(or_1_out));
  Counter counter_1 (
    .clr(rgb_video_1_p1[0]), .clk(rgb_video_1_p1[1]), .Q(counter_1_q));  // open: load, up, count, D, carry
  Multiplexer multiplexer_23 (.in0(comparator_17_eq), .in1(comparator_13_eq));  // open: out, sel
  Comparator #(.width(16)) comparator_13 (
    .a(multiplexer_11_out), .b({X_q_2, X_q}), .eq(comparator_13_eq));  // open: gt, lt
  not not_4 (not_4_out, comparator_13_eq);
  Clock #(.highDuration(5), .lowDuration(5)) clock_2 (.out(clock_2_out));
  Counter #(.max('hffff), .width(16)) counter_2 (
    .clr(rgb_video_1_p1[3]), .clk(multiplexer_24_out), .Q(counter_2_q));  // open: load, up, count, D, carry
  Multiplexer multiplexer_24 (.in1(clock_2_out), .out(multiplexer_24_out), .sel(rgb_video_1_p1[2]));  // open: in0
  ROM #(.dataWidth(48)) rom_1 (.addr(counter_1_q), .data({rom_1_data_2, rom_1_data}));
  ROM #(.addrWidth(16), .dataWidth(17)) rom_2 (.addr(counter_2_q), .data(rom_2_data));
  ROM #(.dataWidth(48), .misaligned("true")) rom_3 (.addr(counter_1_q), .data({rom_3_data_2, rom_3_data}));
  Multiplexer #(.width(16)) multiplexer_25 (
    .in0(divider_1_out), .in1(divider_3_out), .out(multiplexer_25_out), .sel(and_4_out));
  Multiplexer #(.width(16)) multiplexer_26 (
    .in0(divider_2_out), .in1(divider_4_out), .out(multiplexer_26_out), .sel(and_4_out));
  Multiplexer #(.width(16)) multiplexer_27 (
    .in0(divider_3_out), .in1(divider_1_out), .out(multiplexer_27_out), .sel(and_4_out));
  Multiplexer #(.width(16)) multiplexer_28 (
    .in0(divider_4_out), .in1(divider_2_out), .out(multiplexer_28_out), .sel(and_4_out));
  // LedBar #(.inputtype("row"), .matrixcols(16)) DX2: pin names not known; wires that end beside it: DX2_p1
  Subtractor #(.width(16)) subtractor_7 (.a(DX_REG_q), .b(DY2_p1), .out(subtractor_7_out));  // open: bin, bout
  Multiplier #(.mode("twosComplement"), .width(16)) multiplier_9 (
    .a(subtractor_7_out), .b(16'h2), .out(multiplier_9_out));  // open: cin, cout
  Adder #(.width(16)) adder_8 (.a(multiplier_9_out), .b(D2_SUB_q), .out(adder_8_out));  // open: cin, cout
  Adder #(.width(16)) adder_9 (.a(D2_SUB_q), .b(multiplier_10_out), .out(adder_9_out));  // open: cin, cout
  Multiplexer #(.width(16)) multiplexer_29 (
    .in0({16{1'b0}}), .in1(multiplexer_25_out), .out(multiplexer_29_out), .sel(rgb_video_1_p1[4]));
  Subtractor #(.width(16)) subtractor_8 (
    .a(multiplexer_33_out), .b(multiplexer_29_out), .out(DX2_p1));  // open: bin, bout
  Negator #(.width(16)) negator_2 (.in(DX2_p1), .out(negator_2_out));
  Comparator #(.width(16)) comparator_14 (
    .a(D2_SUB_q), .b({16{1'b0}}), .gt(comparator_14_gt), .eq(comparator_14_eq), .lt(comparator_14_lt));
  Register #(.width(1)) register_4 (
    .D(comparator_14_gt), .en(1'b1), .clk(clock_3_out), .Q(register_4_q), .clr(and_15_out));
  Register #(.width(1)) register_5 (
    .D(comparator_14_eq), .en(1'b1), .clk(clock_3_out), .Q(register_5_q), .clr(and_15_out));
  Register #(.width(1)) register_6 (
    .D(comparator_14_lt), .en(1'b1), .clk(clock_3_out), .Q(register_6_q), .clr(and_15_out));
  // RGB_Video #(.height(64), .scale(8), .width(64)) rgb_video_1: pin names not known; wires that end beside it: rgb_video_1_p1[0], clock_1_out, multiplexer_21_out, multiplexer_18_out, multiplexer_20_out, multiplexer_19_out, multiplexer_20_out
  Multiplexer #(.width(16)) multiplexer_30 (
    .in0({16{1'b0}}), .in1(multiplexer_26_out), .out(multiplexer_30_out), .sel(rgb_video_1_p1[4]));
  // LedBar #(.inputtype("row"), .matrixcols(16)) DY2: pin names not known; wires that end beside it: DY2_p1
  Multiplexer #(.width(16)) multiplexer_31 (
    .in0(DX2_p1), .in1(negator_2_out), .out(multiplexer_31_out), .sel(and_13_out));
  Multiplexer #(.width(16)) multiplexer_32 (
    .in0(D2_SUB_q), .in1(adder_8_out), .out(multiplexer_32_out), .sel(register_4_q));
  Adder #(.width(16)) adder_10 (.a({X_SUB_q_2, X_SUB_q}), .b(XI_q), .out(adder_10_out));  // open: cin, cout
  Multiplexer #(.width(16)) multiplexer_33 (
    .in0({16{1'b0}}), .in1(multiplexer_27_out), .out(multiplexer_33_out), .sel(rgb_video_1_p1[4]));
  Subtractor #(.width(16)) subtractor_9 (
    .a(multiplexer_36_out), .b(multiplexer_30_out), .out(DY2_p1));  // open: bin, bout
  Comparator #(.width(16)) comparator_15 (.a(DX2_p1), .b({16{1'b0}}), .lt(comparator_15_lt));  // open: gt, eq
  Register #(.width(16)) DX_REG (
    .D(multiplexer_31_out), .en(rom_5_data[3]), .clk(clock_3_out), .Q(DX_REG_q));  // open: clr
  Multiplier #(.mode("twosComplement"), .width(16)) multiplier_10 (
    .a(DX_REG_q), .b(16'h2), .out(multiplier_10_out));  // open: cin, cout
  Multiplexer #(.width(16)) multiplexer_34 (.in0(D2_q), .in1(adder_9_out), .out(multiplexer_34_out), .sel(or_4_out));
  Multiplexer #(.width(16)) multiplexer_35 (
    .in0({X_SUB_q_2, X_SUB_q}), .in1(adder_10_out), .out(multiplexer_35_out), .sel(and_11_out));
  and and_11 (and_11_out, rom_5_data[12], register_4_q);
  or or_4 (or_4_out, register_5_q, register_6_q);
  Multiplexer #(.width(16)) multiplexer_36 (
    .in0({16{1'b0}}), .in1(multiplexer_28_out), .out(multiplexer_36_out), .sel(rgb_video_1_p1[4]));
  and and_12 (and_12_out, rom_5_data[2], comparator_15_lt);
  and and_13 (and_13_out, comparator_15_lt, rom_5_data[4]);
  Subtractor #(.width(16)) subtractor_10 (
    .a(multiplier_10_out), .b(DY2_p1), .out(subtractor_10_out));  // open: bin, bout
  Multiplexer #(.width(16)) multiplexer_37 (
    .in0(multiplexer_32_out), .in1(multiplexer_34_out), .out(multiplexer_37_out), .sel(rom_5_data[16]));
  Multiplexer #(.width(16)) multiplexer_38 (
    .in0(multiplexer_29_out), .in1(multiplexer_35_out), .out(multiplexer_38_out), .sel(rom_5_data[12]));
  not not_5 (not_5_out, and_12_out);
  Multiplexer #(.width(16)) multiplexer_39 (
    .in0(subtractor_10_out), .in1(multiplexer_37_out), .out(multiplexer_39_out), .sel(rom_5_data[15]));
  Register #(.width(16)) D2 (.D(multiplexer_39_out), .en(rom_5_data[5]), .clk(clock_3_out), .Q(D2_q));  // open: clr
  Register #(.width(16)) XREG (.D(multiplexer_38_out), .en(and_14_out), .clk(clock_3_out), .Q(XREG_q));  // open: clr
  and and_14 (and_14_out, rom_5_data[11], not_6_out);
  Counter #(.max('hffff), .width(16)) XI (
    .clr(rom_5_data[1]), .up(not_5_out), .clk(xor_3_out), .Q(XI_q));  // open: load, count, D, carry
  Clock clock_3 (.out(clock_3_out));
  xor xor_3 (xor_3_out, rom_5_data[0], and_12_out);
  Register #(.width(16)) D2_SUB (.D(D2_q), .en(rom_5_data[14]), .clk(clock_3_out), .Q(D2_SUB_q));  // open: clr
  Register #(.width(16)) X_SUB (
    .D(XREG_q), .en(rom_5_data[13]), .clk(clock_3_out), .Q({X_SUB_q_2, X_SUB_q}));  // open: clr
  Comparator #(.width(16)) comparator_16 (
    .a({X_SUB_q_2, X_SUB_q}), .b(multiplexer_36_out), .eq(comparator_16_eq));  // open: gt, lt
  Clock #(.highDuration(2500), .lowDuration(2500)) clock_4 (.out(clock_4_out));
  not not_6 (not_6_out, comparator_16_eq);
  Multiplexer multiplexer_40 (.in1(clock_4_out), .out(multiplexer_40_out), .sel(dipswitch_1_sw1));  // open: in0
  DipSwitch #(.number(2)) dipswitch_1 (.sw1(dipswitch_1_sw1), .sw2(dipswitch_1_sw2));
  and and_15 (and_15_out, rom_5_data[1], rom_5_data[10]);
  Counter counter_3 (
    .clr(dipswitch_1_sw2), .clk(multiplexer_40_out), .Q(counter_3_q));  // open: load, up, count, D, carry
  LED led_3 (.in(register_4_q));
  buf xor_4 (xor_4_out, rom_5_data[6]);  // XOR_Gate
  Counter #(.max('hffff), .width(16)) Y_CNT (
    .clr(xor_4_out), .load(rom_5_data[8]), .count(not_7_out), .clk(rom_5_data[7]), .D(multiplexer_30_out),
    .Q({Y_CNT_q_2, Y_CNT_q}));  // open: up, carry
  LED led_4 (.in(or_4_out));
  ROM #(.dataWidth(5)) rom_4 (.addr(counter_3_q), .data(rgb_video_1_p1));
  // DipSwitch #(.number(16)) FOV: pin names not known
  Comparator #(.width(16)) comparator_17 (
    .a(multiplexer_36_out), .b({Y_CNT_q_2, Y_CNT_q}), .eq(comparator_17_eq));  // open: gt, lt
  not not_7 (not_7_out, comparator_17_eq);
  Multiplexer multiplexer_41 (.in1(clock_5_out), .out(multiplexer_41_out), .sel(rgb_video_1_p1[2]));  // open: in0
  Clock #(.highDuration(5), .lowDuration(5)) clock_5 (.out(clock_5_out));
  Counter #(.max('hffff), .width(16)) counter_4 (
    .clr(rgb_video_1_p1[3]), .clk(multiplexer_41_out), .Q(counter_4_q));  // open: load, up, count, D, carry
  ROM #(.addrWidth(16), .dataWidth(17)) rom_5 (.addr(counter_4_q), .data(rom_5_data));

  // Notes on the sheet:
  //   x1
  //   y1
  //   x2
  //   y2
  //   x1
  //   y1
  //   x2
  //   B
  //   y2
  //   A
  //   17 - D+(2*(dy-dx)) D+2*dy
  //   LOW
  //   1 - Pulse YI
  //   2 - YI CLR
  //   3 - DY < 0 yi--
  //   4 -DY STR
  //   5 - DY < 0 invert
  //   6 - D IN
  //   7 - X CLR
  //   8 - X UP
  //   9 - X LD
  //   10 - PLT
  //   11 - RST screen
  //   12 - Y IN
  //   13 - Y y1/yi
  //   14 - Y sub IN
  //   15 - D sub IN
  //   16 - D sub/d2
  //   D > 0
  //   ELSE
  //   contents of rom_1 (hex, n*v repeats v):
  //   240038 0 240008 0 2000220020 0 2000220020 0 60038 0 60008 0 2000020020 0 2000020020 0 2c0020 0
  //   240008 0 240038 0 2000220020
  //   A
  //   contents of rom_2 (hex, n*v repeats v):
  //   6c62 1 4 0 4 18 20 4000 800 2000 180 200 1800 2000 8020 18020 4000 80 200 1800 2000 8020 18020 4000
  //   80 200 1800 2000 8020 18020 4000 80 200 1800 2000 8020 18020 4000 80 200 1800 2000 8020 18020 4000
  //   80 200 1800 2000 8020 18020 4000 80 200 1800 2000 8020 18020 4000 80 200 1800 2000 8020 18020 4000
  //   80 200 1800 2000 8020 18020 4000 80 200 1800 2000 8020 18020 4000 80 200 1800 2000 8020 18020 4000
  //   80 200 1800 2000 8020 18020 4000 80 200 1800 2000 8020 18020 4000 80 200 1800 2000 8020 18020 4000
  //   80 200 1800 2000 8020 18020 4000 80 200 1800 2000 8020 18020 4000 80 200 1800 2000 8020 18020 4000
  //   80 200 1800 2000 8020 18020 4000 80 200 1800 2000 8020 18020 4000 80 200 1800 2000 8020 18020 4000
  //   80 200 1800 2000 8020 18020 4000 80 200 1800 2000 8020 18020 4000 80 200 1800 2000 8020 18020 4000
  //   80 200 1800 2000 8020 18020 4000 80 200 1800 2000 8020 18020 4000 80 200 1800 2000 8020 18020 4000
  //   80 200 1800 2000 8020 18020 4000 80 200 1800 2000 8020 18020 4000 80 200 1800 2000 8020 18020 4000
  //   80 200 1800 2000 8020 18020 4000 80 200 1800 2000 8020 18020 4000 80 200 1800 2000 8020 18020 4000
  //   80 200 1800 2000 8020 18020 4000 80 200 1800 2000 8020 18020 4000 80 200 1800 2000 8020 18020 4000
  //   80 200 1800 2000 8020 18020 4000 80 200 1800 2000 8020 18020 4000 80 200 1800 2000 8020 18020 4000
  //   80 200 1800 2000 8020 18020 4000 80 200 1800 2000 8020 18020 4000 80 200 1800 2000 8020 18020 4000
  //   80 200 1800 2000 8020 18020 4000 80 200 1800 2000 8020 18020 4000 80 200 1800 2000 8020 18020 4000
  //   80 200 1800 2000 8020 18020 4000 80 200 1800 2000 8020 18020 4000 80 200 1800 2000 8020 18020 4000
  //   80 200 1800 2000 8020 18020 4000 80 200 1800 2000 8020 18020 4000 80 200 1800 2000 8020 18020 4000
  //   80 200 1800 2000 8020 18020 4000 80 200 1800 2000 8020 18020 4000 80 200 1800 2000 8020 18020 4000
  //   80 200 1800 2000 8020 18020 4000 80 200 1800 2000 8020 18020 4000 80 200 1800 2000 8020 18020 4000
  //   80 200 1800 2000 8020 18020 4000 80 200 1800 2000 8020 18020 4000 80
  //   contents of rom_3 (hex, n*v repeats v):
  //   2c0020 0 2c0020 0 240008 0 240038 0 e0020 0 e0020 0 60008 0 60038 0 e0020 0 60008 0 60038 0
  //   2000020020
  //   B
  //   x1
  //   y1
  //   x2
  //   y2
  //   x1
  //   y1
  //   x2
  //   y2
  //   1 - CLR LN
  //   2 - In to GPU
  //   3 - NXT LN
  //   4 - CLK ON
  //   5 - CLR
  //   1
  //   17 - D+(2*(dy-dx)) D+2*dy
  //   5
  //   HIGH
  //   D > 0
  //   1 - Pulse YI
  //   2 - YI CLR
  //   3 - DY < 0 yi--
  //   4 -DY STR
  //   5 - DY < 0 invert
  //   6 - D IN
  //   7 - X CLR
  //   8 - X UP
  //   9 - X LD
  //   10 - PLT
  //   11 - RST screen
  //   12 - Y IN
  //   13 - Y y1/yi
  //   14 - Y sub IN
  //   15 - D sub IN
  //   16 - D sub/d2
  //   ELSE
  //   contents of rom_4 (hex, n*v repeats v):
  //   10 1 18 14 2 18 14 2 18 14 2 18 14 2 18 14 2 18 14 2 18 14 2 18 14 2 18 14 2 18 14 2 18 14 2 18 14 2
  //   18 14 2 18 14 2 18 14 2 18 14 2 18 14 2 18 14 2 18 14 2 18 14 2 18 14 2 18 14 2 18 14 2 18 14 2 18
  //   14
  //   contents of rom_5 (hex, n*v repeats v):
  //   6c62 1 4 0 4 18 20 4000 800 2000 180 200 1800 2000 8020 18020 4000 80 200 1800 2000 8020 18020 4000
  //   80 200 1800 2000 8020 18020 4000 80 200 1800 2000 8020 18020 4000 80 200 1800 2000 8020 18020 4000
  //   80 200 1800 2000 8020 18020 4000 80 200 1800 2000 8020 18020 4000 80 200 1800 2000 8020 18020 4000
  //   80 200 1800 2000 8020 18020 4000 80 200 1800 2000 8020 18020 4000 80 200 1800 2000 8020 18020 4000
  //   80 200 1800 2000 8020 18020 4000 80 200 1800 2000 8020 18020 4000 80 200 1800 2000 8020 18020 4000
  //   80 200 1800 2000 8020 18020 4000 80 200 1800 2000 8020 18020 4000 80 200 1800 2000 8020 18020 4000
  //   80 200 1800 2000 8020 18020 4000 80 200 1800 2000 8020 18020 4000 80 200 1800 2000 8020 18020 4000
  //   80 200 1800 2000 8020 18020 4000 80 200 1800 2000 8020 18020 4000 80 200 1800 2000 8020 18020 4000
  //   80 200 1800 2000 8020 18020 4000 80 200 1800 2000 8020 18020 4000 80 200 1800 2000 8020 18020 4000
  //   80 200 1800 2000 8020 18020 4000 80 200 1800 2000 8020 18020 4000 80 200 1800 2000 8020 18020 4000
  //   80 200 1800 2000 8020 18020 4000 80 200 1800 2000 8020 18020 4000 80 200 1800 2000 8020 18020 4000
  //   80 200 1800 2000 8020 18020 4000 80 200 1800 2000 8020 18020 4000 80 200 1800 2000 8020 18020 4000
  //   80 200 1800 2000 8020 18020 4000 80 200 1800 2000 8020 18020 4000 80 200 1800 2000 8020 18020 4000
  //   80 200 1800 2000 8020 18020 4000 80 200 1800 2000 8020 18020 4000 80 200 1800 2000 8020 18020 4000
  //   80 200 1800 2000 8020 18020 4000 80 200 1800 2000 8020 18020 4000 80 200 1800 2000 8020 18020 4000
  //   80 200 1800 2000 8020 18020 4000 80 200 1800 2000 8020 18020 4000 80 200 1800 2000 8020 18020 4000
  //   80 200 1800 2000 8020 18020 4000 80 200 1800 2000 8020 18020 4000 80 200 1800 2000 8020 18020 4000
  //   80 200 1800 2000 8020 18020 4000 80 200 1800 2000 8020 18020 4000 80 200 1800 2000 8020 18020 4000
  //   80 200 1800 2000 8020 18020 4000 80 200 1800 2000 8020 18020 4000 80 200 1800 2000 8020 18020 4000
  //   80 200 1800 2000 8020 18020 4000 80 200 1800 2000 8020 18020 4000 80
endmodule
